# Fritzing sketch ttp224n-esquema-ligacao-fritzen-um (saved by Fritzing 0.9.2b)

parts:
  Componente1 = Arduino Uno (Rev3)
  JP1 = Header 6 [package=molex-1x6-ra_lock]

nets:
  N1: Componente1.D2, JP1.3
  N2: Componente1.D3_PWM, JP1.4
  N3: Componente1.D4, JP1.5
  N4: Componente1.D5_PWM, JP1.6
  N5: Componente1.5V, JP1.1
  N6: Componente1.GND, JP1.2

notes:
  +5V
  GND
  OUT4
  OUT1
